// Logisim project cpu.circ as structural Verilog: 4 circuits, main circuit main
module main (
  input  [31:0] INSTRUCTION,
  input  CLOCK,
  output [31:0] PROGRAM_COUNTER,
  output [31:0] ra,
  output [31:0] sp,
  output [31:0] t0,
  output [31:0] t1,
  output [31:0] t2,
  output [31:0] s0,
  output [31:0] s1,
  output [31:0] a0
);

  wire a_sel, b_sel, breq, brlt, brun, memRW, nop, pc_sel, regWen;
  wire [1:0] controls_1_out_16, load_sel, wb_sel;
  wire [3:0] alu_sel;
  wire [7:0] bitselector_1_out;
  wire [15:0] multiplexer_6_out;
  wire [31:0] adder_2_out, alu_res, bit_extender_1_out, bit_extender_2_out, DataA, DataB, imm_result,
       instr_save, mem, multiplexer_1_out, multiplexer_2_out, multiplexer_3_out, multiplexer_4_out,
       multiplexer_5_out, PC_plus_4, saved_PC, wb;

  Multiplexer #(.width(32), .enable("false")) multiplexer_1 (
    .in0(PC_plus_4), .in1(alu_res), .out(multiplexer_1_out), .sel(pc_sel));
  Register #(.width(32)) PC (.D(multiplexer_1_out), .clk(CLOCK), .Q(PROGRAM_COUNTER));  // open: en, clr
  Multiplexer #(.width(32), .enable("false")) multiplexer_2 (
    .in0(INSTRUCTION), .in1({32{1'b0}}), .out(multiplexer_2_out), .sel(nop));
  Adder #(.width(32)) adder_1 (.a(PROGRAM_COUNTER), .b(32'h4), .out(PC_plus_4));  // open: cin, cout
  Register #(.width(32)) register_1 (.D(multiplexer_2_out), .clk(CLOCK), .Q(instr_save));  // open: en, clr
  Register #(.width(32)) register_2 (.D(PROGRAM_COUNTER), .clk(CLOCK), .Q(saved_PC));  // open: en, clr
  controls controls_1 (
    .instr(instr_save), .in_2(breq), .in_3(brlt), .out_4(breq), .out_5(brlt), .out_6(pc_sel),
    .out_7(imm_result), .out_8(brun), .out_9(a_sel), .out_10(b_sel), .out_11(alu_sel), .out_12(memRW),
    .out_13(regWen), .out_14(wb_sel), .out_15(nop), .out_16(controls_1_out_16), .out_17(load_sel));
  branch_comparator branch_comparator_1 (.DataA(DataA), .DataB(DataB), .brun(brun), .breq(breq), .brlt(brlt));
  regfile_main RegFile (
    .rs2(instr_save[24:20]), .rd(instr_save[11:7]), .Read_Data_1(DataA), .Read_Data_2(DataB), .ra(ra),
    .sp(sp), .t0(t0), .t1(t1), .t2(t2), .s0(s0), .s1(s1), .a0(a0), .rs1(instr_save[19:15]), .Write_Data(wb),
    .RegWEn(regWen), .clk(CLOCK));
  Adder #(.width(32)) adder_2 (.a(saved_PC), .b(32'h4), .out(adder_2_out));  // open: cin, cout
  Multiplexer #(.width(32), .enable("false")) multiplexer_3 (
    .in0(DataA), .in1(saved_PC), .out(multiplexer_3_out), .sel(a_sel));
  Multiplexer #(.width(32), .enable("false")) multiplexer_4 (
    .in0(DataB), .in1(imm_result), .out(multiplexer_4_out), .sel(b_sel));
  Multiplexer #(.select(2), .width(32), .enable("false")) multiplexer_5 (
    .in0(mem), .in1(alu_res), .in2(adder_2_out), .out(multiplexer_5_out), .sel(wb_sel));  // open: in3
  alu Arithmetic_Logic_Unit (.B(multiplexer_4_out), .Result(alu_res), .A(multiplexer_3_out), .ALUSel(alu_sel));
  BitSelector #(.width(32), .group(8)) bitselector_1 (
    .in(multiplexer_5_out), .out(bitselector_1_out), .sel(alu_res[1:0]));
  Multiplexer #(.select(2), .width(16), .enable("false")) multiplexer_6 (
    .in0(multiplexer_5_out[15:0]), .in1(multiplexer_5_out[23:8]), .in2(multiplexer_5_out[31:16]),
    .in3(multiplexer_5_out[31:16]), .out(multiplexer_6_out), .sel(alu_res[1:0]));
  assign bit_extender_1_out = {{24{bitselector_1_out[7]}}, bitselector_1_out};  // Bit_Extender bit_extender_1
  assign bit_extender_2_out = {{16{multiplexer_6_out[15]}}, multiplexer_6_out};  // Bit_Extender bit_extender_2
  Multiplexer #(.select(2), .width(32), .enable("false")) multiplexer_7 (
    .in0(multiplexer_5_out), .in1(bit_extender_1_out), .in2(bit_extender_2_out), .out(wb), .sel(load_sel));  // open: in3
  // mem_main DMEM: pin names not known; wires that end beside it: alu_res, DataB, CLOCK, memRW, mem

  // Other names for the same wires on the sheet: offset[1:0] = alu_res[1:0]; clk = CLOCK; rd[4:0] = instr_save[11:7];
  //   rs1[4:0] = instr_save[19:15]; rs2[4:0] = instr_save[24:20]

  // Notes on the sheet:
  //   Output
  //   IMEM (do **NOT** move this)
  //   Inputs
  //   Inputs/Outputs for testing. Do **NOT** move these.
endmodule

module imm_generator (
  input  [31:0] in_1,
  input  [2:0] in_2,
  output [31:0] out_3
);

  wire [11:0] bit_extender_1_out, U_imm;
  wire [31:0] I_imm, result_i, result_s, result_sb, S_imm, SB_imm, UJ_imm;
  wire [31:1] result_uj;
  wire [31:12] result_u;

  assign bit_extender_1_out = {{11{1'b0}}, 1'b0};  // Bit_Extender bit_extender_1
  Demultiplexer #(.select(3), .width(32), .enable("false")) demultiplexer_1 (
    .out0(I_imm), .out1(S_imm), .out2(SB_imm), .out3({result_u, U_imm}),
    .out4({UJ_imm[31], result_uj[10:1], result_uj[11], result_uj[19:12], UJ_imm[11:0]}), .in(in_1), .sel(in_2));  // open: out5, out6, out7
  assign result_uj[31:20] = {{11{UJ_imm[31]}}, UJ_imm[31]};  // Bit_Extender bit_extender_2
  assign result_i = {{20{I_imm[31]}}, I_imm[31:20]};  // Bit_Extender bit_extender_3
  assign result_s = {{20{S_imm[31]}}, {S_imm[31:25], S_imm[11:7]}};  // Bit_Extender bit_extender_4
  assign result_sb = {{19{SB_imm[31]}}, {SB_imm[31], SB_imm[7], SB_imm[30:25], SB_imm[11:8], 1'b0}};  // Bit_Extender bit_extender_5
  assign out_3 = result_i | result_s | result_sb | {result_u, {12{1'b0}}} | {result_uj, 1'b0};  // OR_Gate or_1, 32 bits wide

  // Other names for the same wires on the sheet: result[31:0] = out_3; U_imm[31:12] = result_u;
  //   UJ_imm[30:12] = {result_uj[10:1], result_uj[11], result_uj[19:12]}
endmodule

module controls (
  input  [31:0] instr,
  input  in_2,
  input  in_3,
  output out_4,
  output out_5,
  output out_6,
  output [31:0] out_7,
  output out_8,
  output out_9,
  output out_10,
  output [3:0] out_11,
  output out_12,
  output out_13,
  output [1:0] out_14,
  output out_15,
  output [1:0] out_16,
  output [1:0] out_17
);

  wire and_1_out, and_2_out, and_3_out, and_4_out, and_5_out, and_6_out, comparator_2_eq, comparator_3_eq,
       comparator_4_eq, comparator_9_eq, comparator_10_eq, comparator_11_eq, comparator_12_eq,
       comparator_13_eq, comparator_14_eq, comparator_15_eq, comparator_16_eq, comparator_17_eq,
       comparator_18_eq, comparator_19_eq, I, not_1_out, or_5_out, or_7_out, or_8_out, or_9_out, R, SB, U, UJ;
  wire [1:0] bit_extender_1_out, bit_extender_2_out, bit_extender_3_out, bit_extender_4_out,
       multiplier_1_out, multiplier_2_out;
  wire [2:0] b_func3, load_func3, s_func3;
  wire [3:0] multiplexer_1_out;
  wire [4:0] r_f3f7_sel;
  wire [6:0] b_func7;
  wire [6:1] r_func7;
  wire [24:0] b_instr, r_instr;
  wire [31:0] i_instr, imm_b, imm_i, imm_j, imm_jalr, imm_load, imm_s, imm_u, j_instr, jalr_instr,
       load_instr, ops_1, ops_2, s_instr, u_instr;

  Comparator #(.width(7)) comparator_1 (.a(instr[6:0]), .b(7'b0110011), .eq(R));  // open: gt, lt
  Comparator #(.width(7)) comparator_2 (.a(instr[6:0]), .b(7'b0000011), .eq(comparator_2_eq));  // open: gt, lt
  Comparator #(.width(7)) comparator_3 (.a(instr[6:0]), .b(7'b0010011), .eq(comparator_3_eq));  // open: gt, lt
  Comparator #(.width(7)) comparator_4 (.a(instr[6:0]), .b(7'b1100111), .eq(comparator_4_eq));  // open: gt, lt
  Comparator #(.width(7)) comparator_5 (.a(instr[6:0]), .b(7'b0100011), .eq(out_12));  // open: gt, lt
  Comparator #(.width(7)) comparator_6 (.a(instr[6:0]), .b(7'b1100011), .eq(SB));  // open: gt, lt
  Comparator #(.width(7)) comparator_7 (.a(instr[6:0]), .b(7'b1101111), .eq(UJ));  // open: gt, lt
  Comparator #(.width(7)) comparator_8 (.a(instr[6:0]), .b(7'b0110111), .eq(U));  // open: gt, lt
  or or_1 (I, comparator_2_eq, comparator_3_eq, comparator_4_eq);
  Comparator #(.width(3)) comparator_9 (.a(load_func3), .b(3'b000), .eq(comparator_9_eq));  // open: gt, lt
  Comparator #(.width(7)) comparator_10 (.a(instr[6:0]), .b(7'b0000011), .eq(comparator_10_eq));  // open: gt, lt
  Comparator #(.width(3)) comparator_11 (.a(load_func3), .b(3'b001), .eq(comparator_11_eq));  // open: gt, lt
  Comparator #(.width(7)) comparator_12 (.a(instr[6:0]), .b(7'b0000011), .eq(comparator_12_eq));  // open: gt, lt
  not not_1 (not_1_out, in_2);
  and and_1 (and_1_out, comparator_9_eq, instr[0], comparator_10_eq);
  and and_2 (and_2_out, comparator_11_eq, instr[0], comparator_12_eq);
  Demultiplexer #(.select(3), .width(32), .enable("false")) demultiplexer_1 (
    .out3(ops_1), .out7(ops_2), .in(instr), .sel(instr[2:0]));  // open: out0, out1, out2, out4, out5, out6
  Comparator #(.width(3)) comparator_13 (.a(b_func3), .b(3'b000), .eq(comparator_13_eq));  // open: gt, lt
  Comparator #(.width(3)) comparator_14 (.a(b_func3), .b(3'b001), .eq(comparator_14_eq));  // open: gt, lt
  Comparator #(.width(3)) comparator_15 (.a(b_func3), .b(3'b100), .eq(comparator_15_eq));  // open: gt, lt
  Comparator #(.width(3)) comparator_16 (.a(b_func3), .b(3'b110), .eq(comparator_16_eq));  // open: gt, lt
  or or_2 (out_9, SB, UJ);
  or or_3 (out_10, I, out_12, SB, U, UJ);
  or or_4 (out_13, R, I, U, UJ);
  assign bit_extender_1_out = {{1{1'b0}}, and_1_out};  // Bit_Extender bit_extender_1
  assign bit_extender_2_out = {{1{1'b0}}, and_2_out};  // Bit_Extender bit_extender_2
  Multiplexer #(.select(5), .width(4), .enable("false")) multiplexer_1 (
    .in0(4'b0000), .in1(4'b1010), .in2(4'b1100), .in4(4'b0110), .in5(4'b1110), .in8(4'b0111), .in13(4'b1011),
    .in16(4'b0011), .in20(4'b0100), .in21(4'b1000), .in24(4'b0010), .in28(4'b0001), .in29(4'b1001),
    .out(multiplexer_1_out), .sel(r_f3f7_sel));  // open: in3, in6, in7, in9, in10, in11, in12, in14, in15, in17, in18, in19, in22, in23, in25, in26, in27, in30, in31
  Comparator #(.width(7)) comparator_17 (.a(instr[6:0]), .b(7'b1100111), .eq(comparator_17_eq));  // open: gt, lt
  and and_3 (and_3_out, not_1_out, comparator_14_eq);
  Multiplier #(.width(2)) multiplier_1 (.a(bit_extender_2_out), .b(2'b10), .out(multiplier_1_out));  // open: cin, cout
  and and_4 (and_4_out, in_2, comparator_13_eq);
  or or_5 (or_5_out, comparator_15_eq, comparator_16_eq);
  assign out_17 = bit_extender_1_out | multiplier_1_out;  // OR_Gate or_6, 2 bits wide
  Multiplexer #(.width(4), .enable("false")) multiplexer_2 (
    .in0(multiplexer_1_out), .in1(4'b1101), .out(out_11), .sel(U));
  and and_5 (and_5_out, in_3, or_5_out);
  Comparator #(.width(7)) comparator_18 (.a(instr[6:0]), .b(7'b0010011), .eq(comparator_18_eq));  // open: gt, lt
  Comparator #(.width(7)) comparator_19 (.a(instr[6:0]), .b(7'b1100111), .eq(comparator_19_eq));  // open: gt, lt
  Demultiplexer #(.select(4), .width(32), .enable("false")) demultiplexer_2 (
    .out0({load_instr[31:15], load_func3, load_instr[11:0]}), .out2(i_instr),
    .out4({s_instr[31:15], s_func3, s_instr[11:0]}),
    .out6({r_func7[6], r_f3f7_sel[1], r_func7[4:1], r_f3f7_sel[0], r_instr[24:15], r_f3f7_sel[4:2], r_instr[11:0]}),
    .out12({b_func7, b_instr[24:15], b_func3, b_instr[11:0]}), .in(ops_1), .sel(instr[6:3]));  // open: out1, out3, out5, out7, out8, out9, out10, out11, out13, out14, out15
  or or_7 (or_7_out, and_4_out, and_3_out, and_5_out);
  Multiplexer #(.select(3), .enable("false")) multiplexer_3 (
    .in6(1'b1), .out(out_8), .sel(b_func3));  // open: in0, in1, in2, in3, in4, in5, in7
  or or_8 (or_8_out, comparator_18_eq, R, U);
  and and_6 (and_6_out, or_7_out, SB);
  assign bit_extender_3_out = {{1{1'b0}}, or_8_out};  // Bit_Extender bit_extender_3
  assign bit_extender_4_out = {{1{1'b0}}, or_9_out};  // Bit_Extender bit_extender_4
  or or_9 (or_9_out, UJ, comparator_19_eq);
  or or_10 (out_6, UJ, comparator_17_eq, and_6_out);
  Multiplier #(.width(2)) multiplier_2 (.a(bit_extender_4_out), .b(2'b10), .out(multiplier_2_out));  // open: cin, cout
  Demultiplexer #(.select(4), .width(32), .enable("false")) demultiplexer_3 (
    .out6(u_instr), .out12(jalr_instr), .out13(j_instr), .in(ops_2), .sel(instr[6:3]));  // open: out0, out1, out2, out3, out4, out5, out7, out8, out9, out10, out11, out14, out15
  assign out_14 = bit_extender_3_out | multiplier_2_out;  // OR_Gate or_11, 2 bits wide
  imm_generator imm_generator_1 (
    .in_1({b_func7, b_instr[24:15], b_func3, b_instr[11:0]}), .in_2(3'b010), .out_3(imm_b));
  imm_generator imm_generator_2 (.in_1({s_instr[31:15], s_func3, s_instr[11:0]}), .in_2(3'b001), .out_3(imm_s));
  imm_generator imm_generator_3 (.in_1(jalr_instr), .in_2(3'b000), .out_3(imm_jalr));
  assign out_7 = imm_b | imm_s | imm_jalr | imm_j | imm_u | imm_i | imm_load;  // OR_Gate or_12, 32 bits wide
  imm_generator imm_generator_4 (.in_1(i_instr), .in_2(3'b000), .out_3(imm_i));
  imm_generator imm_generator_5 (.in_1(u_instr), .in_2(3'b011), .out_3(imm_u));
  imm_generator imm_generator_6 (.in_1(j_instr), .in_2(3'b100), .out_3(imm_j));
  imm_generator imm_generator_7 (
    .in_1({load_instr[31:15], load_func3, load_instr[11:0]}), .in_2(3'b000), .out_3(imm_load));

  assign out_15 = out_6;
  assign out_16 = instr[21:20];

  // Other names for the same wires on the sheet: a_sel = out_9; alu_sel[3:0] = out_11;
  //   b_instr (some bits) = {b_func7, b_func3}; b_sel = out_10; beq = in_2; blt = in_3; breq = out_4; brlt = out_5;
  //   brun = out_8; imm[31:0] = out_7; bottom3_oc[2:0] = instr[2:0]; instr_save[31:0] = instr; nop_check = instr[0];
  //   opcode[6:0] = instr[6:0]; top4_oc[3:0] = instr[6:3]; offset[1:0] = instr[21:20]; load_instr[14:12] = load_func3;
  //   load_sel[1:0] = out_17; memRW = out_12; S = out_12; nop = out_6; pc_sel = out_6; r_func3[2:0] = r_f3f7_sel[4:2];
  //   r_instr (some bits) = {r_func7[6], r_f3f7_sel[1], r_func7[4:1], r_f3f7_sel[0], r_f3f7_sel[4:2]};
  //   r_func7 (some bits) = r_f3f7_sel[1:0]; regWen = out_13; s_instr[14:12] = s_func3; wb_sel[1:0] = out_14
endmodule

module branch_comparator (
  input  [31:0] DataA,
  input  [31:0] DataB,
  input  brun,
  output breq,
  output brlt
);

  wire eq1, eq2, lt1, lt2;

  Comparator #(.width(32)) comparator_1 (.a(DataA), .b(DataB), .eq(eq1), .lt(lt1));  // open: gt
  Comparator #(.width(32), .mode("unsigned")) comparator_2 (.a(DataA), .b(DataB), .eq(eq2), .lt(lt2));  // open: gt
  Multiplexer #(.enable("false")) multiplexer_1 (.in0(eq1), .in1(eq2), .out(breq), .sel(brun));
  Multiplexer #(.enable("false")) multiplexer_2 (.in0(lt1), .in1(lt2), .out(brlt), .sel(brun));
endmodule
