// Logisim project alu.circ as structural Verilog: 1 circuit, main circuit alu
module alu (
  input  [31:0] A,
  input  [31:0] B,
  input  [3:0] ALUSel,
  output [31:0] Result
);

  wire adder_4_cout, comparator_1_lt, signResult;
  wire [31:0] A0, A1, A2, A3, A4, A5, A6, A7, A8, A9, A10, A11, A12, A13, A14, A14flip, add0, adder_1_out,
       adder_2_out, adder_5_out, and1, B0, B1, B2, B3, B4, B5, B6, B7, B8, B9, B10, B11, B12, B13, B14,
       B14flip, divu8, lower32, mul10, mulh14, mulhu11, not_1_out, not_2_out, not_3_out, not_4_out, or2,
       remu9, sll6, slt7, sra5, srl4, sub12, upper32, xor3;

  Demultiplexer #(.select(4), .width(32), .enable("false")) demultiplexer_1 (
    .out0(A0), .out1(A1), .out2(A2), .out3(A3), .out4(A4), .out5(A5), .out6(A6), .out7(A7), .out8(A8),
    .out9(A9), .out10(A10), .out11(A11), .out12(A12), .out13(A13), .out14(A14), .in(A), .sel(ALUSel));  // open: out15
  Demultiplexer #(.select(4), .width(32), .enable("false")) demultiplexer_2 (
    .out0(B0), .out1(B1), .out2(B2), .out3(B3), .out4(B4), .out5(B5), .out6(B6), .out7(B7), .out8(B8),
    .out9(B9), .out10(B10), .out11(B11), .out12(B12), .out13(B13), .out14(B14), .in(B), .sel(ALUSel));  // open: out15
  assign not_1_out = ~A14;  // NOT_Gate not_1, 32 bits wide
  assign not_2_out = ~B14;  // NOT_Gate not_2, 32 bits wide
  Multiplexer #(.width(32), .enable("false")) multiplexer_1 (
    .in0(A14), .in1(adder_1_out), .out(A14flip), .sel(A14[31]));
  Adder #(.width(32)) adder_1 (.a(32'h1), .b(not_1_out), .out(adder_1_out));  // open: cin, cout
  Multiplexer #(.width(32), .enable("false")) multiplexer_2 (
    .in0(B14), .in1(adder_2_out), .out(B14flip), .sel(B14[31]));
  Adder #(.width(32)) adder_2 (.a(32'h1), .b(not_2_out), .out(adder_2_out));  // open: cin, cout
  Adder #(.width(32)) adder_3 (.a(A0), .b(B0), .out(add0));  // open: cin, cout
  assign and1 = A1 & B1;  // AND_Gate and_1, 32 bits wide
  assign or2 = A2 | B2;  // OR_Gate or_1, 32 bits wide
  assign xor3 = A3 ^ B3;  // XOR_Gate xor_1, 32 bits wide
  Shifter #(.width(32), .shift("lr")) shifter_1 (.in(A4), .\dist (B4[4:0]), .out(srl4));
  Shifter #(.width(32), .shift("ar")) shifter_2 (.in(A5), .\dist (B5[4:0]), .out(sra5));
  Shifter #(.width(32)) shifter_3 (.in(A6), .\dist (B6[4:0]), .out(sll6));
  Comparator #(.width(32)) comparator_1 (.a(A7), .b(B7), .lt(comparator_1_lt));  // open: gt, eq
  assign slt7 = {{31{1'b0}}, comparator_1_lt};  // Bit_Extender bit_extender_1
  Divider #(.width(32)) divider_1 (.a(A8), .b(B8), .out(divu8));  // open: upper, rem
  Divider #(.width(32)) divider_2 (.a(A9), .b(B9), .rem(remu9));  // open: out, upper
  Multiplier #(.width(32)) multiplier_1 (.a(A10), .b(B10), .out(mul10));  // open: cin, cout
  Multiplier #(.width(32)) multiplier_2 (.a(A11), .b(B11), .cout(mulhu11));  // open: out, cin
  Subtractor #(.width(32)) subtractor_1 (.a(A12), .b(B12), .out(sub12));  // open: bin, bout
  xor xor_2 (signResult, A14[31], B14[31]);
  assign not_3_out = ~lower32;  // NOT_Gate not_3, 32 bits wide
  assign not_4_out = ~upper32;  // NOT_Gate not_4, 32 bits wide
  Multiplier #(.width(32)) multiplier_3 (.a(A14flip), .b(B14flip), .out(lower32), .cout(upper32));  // open: cin
  Adder #(.width(32)) adder_4 (.a(32'h1), .b(not_3_out), .cout(adder_4_cout));  // open: out, cin
  Adder #(.width(32)) adder_5 (.a({32{1'b0}}), .b(not_4_out), .out(adder_5_out), .cin(adder_4_cout));  // open: cout
  Multiplexer #(.width(32), .enable("false")) multiplexer_3 (
    .in0(upper32), .in1(adder_5_out), .out(mulh14), .sel(signResult));
  Multiplexer #(.select(4), .width(32), .enable("false")) multiplexer_4 (
    .in0(add0), .in1(and1), .in2(or2), .in3(xor3), .in4(srl4), .in5(sra5), .in6(sll6), .in7(slt7),
    .in8(divu8), .in9(remu9), .in10(mul10), .in11(mulhu11), .in12(sub12), .in13(B13), .in14(mulh14),
    .out(Result), .sel(ALUSel));  // open: in15

  // Other names for the same wires on the sheet: A14_rem[30:0] = A14[30:0]; signA = A14[31];
  //   B14_rem[30:0] = B14[30:0]; signB = B14[31]; bsel13[31:0] = B13

  // Notes on the sheet:
  //   INPUTS to your circuit
  //   DON'T CHANGE THE LOCATIONS OF THE INPUTS AND OUTPUTS!
  //   OUTPUT from your circuit
endmodule
